# Fritzing sketch Circuit (saved by Fritzing 0.9.5d)
breadboards: 1

parts:
  Raspberry_Pi_1 = Raspberry Pi 3 [part_number=RPI-3-V1.2]
  ZS-042_RTC1 = ZS-042 RTC Module

nets:
  N1: Raspberry_Pi_1.GPIO2, ZS-042_RTC1.SDA
  N2: Raspberry_Pi_1.GPIO3, ZS-042_RTC1.SCL
  GND: Raspberry_Pi_1.GND, ZS-042_RTC1.GND
  5V: Raspberry_Pi_1.5V, ZS-042_RTC1.VCC
